# Fritzing sketch ESP32-Devkit-v1-30pin (saved by Fritzing 0.9.9b)

parts:
  U1 = ESP32 DEVKIT V1 DOIT [part_number=ESP32S-HiLetgo]
  U2 = Adafruit BNO055 STEMMA QT [part_number="Adafruit #4646"]
  Part1 = GP-20U7
  C1 = Electrolytic Capacitor [capacitance=10µF voltage=35V package="100 mil [THT, electrolytic]"]

nets:
  N1: U1.3.3, Part1.VCC, C1.+
  GND: U1.GND, U2.GND, Part1.GND, C1.-
  N2: U1.GPIO4, U2.VCC
  N3: U1.GPIO16, Part1.TX
  N4: U1.GPIO21, U2.SDA
  N5: U1.GPIO22, U2.SCL

custom parts:
  ESP32 DEVKIT V1 DOIT: 30GPIO Version
  Adafruit BNO055 STEMMA QT: If you've ever ordered and wire up a 9-DOF sensor, chances are you've also realized the challenge of turning the sensor data from an accelerometer, gyroscope, and magnetometer into actual "3D space orientation"! Orientation is a hard problem to solve. The sensor fusion algorithms (the secret sauce that blends accelerometer, magnetometer, and gyroscope data into stable three-axis orientation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
